# Fritzing sketch alarmeF (saved by Fritzing 0.9.3b)
breadboards: 1

parts:
  HC-SR04_Sensor_1 = HC-SR04 Ultrasonic Distance Sensor
  S1 = Momentary Switch [package=ksa_sealed_tac_switch]
  S2 = Momentary Switch [package=ksa_sealed_tac_switch]
  M1 = DC Motor
  Matrix_keypad2 = KEYPAD 4x4
  R1 = Resistor [tolerance=±5% resistance=330 package=THT]
  R2 = Resistor [tolerance=±5% resistance=330 package=THT]
  R3 = Resistor [tolerance=±5% resistance=330 package=THT]
  J1 = Piezo Speaker
  S3 = H-Bridge with L298N
  Componente1 = Arduino Mega 2560 (Rev3)
  R4 = Resistor [tolerance=±20% resistance=330 package=THT]
  S4 = Momentary Switch [package=ksa_sealed_tac_switch]

nets:
  5V: HC-SR04_Sensor_1.VCC, S3.5V, Componente1.5V
  N1: HC-SR04_Sensor_1.TRIG, Componente1.D37
  N2: HC-SR04_Sensor_1.ECHO, Componente1.D41
  GND: HC-SR04_Sensor_1.GND, R1.Pin_0, R3.Pin_1, S3.GND, Componente1.GND, R4.Pin_1
  N3: S1.1, S1.3, R2.Pin_0, Componente1.D45
  N4: S1.2, S1.4
  N5: S2.1, S2.3, R3.Pin_0, Componente1.D49
  N6: S2.2, S2.4, S4.2, S4.4
  N7: M1.pin_1, S3.OUT4-Motor2
  N8: M1.pin_2, S3.OUT3-Motor2
  N9: Matrix_keypad2.col1, Componente1.D24
  N10: Matrix_keypad2.col2, Componente1.D4_PWM
  N11: Matrix_keypad2.col3, Componente1.D2_PWM
  N12: Matrix_keypad2.col4, Componente1.D6_PWM
  N13: Matrix_keypad2.row1, Componente1.D7_PWM
  N14: Matrix_keypad2.row2, Componente1.D8_PWM
  N15: Matrix_keypad2.row3, Componente1.D10_PWM
  N16: Matrix_keypad2.row4, Componente1.D5_PWM
  N17: R1.Pin_1, J1.pin1
  N18: J1.pin2, Componente1.D33
  N19: S3.IN3, Componente1.A2
  N20: S3.IN4, Componente1.A1
  N21: Componente1.D53, R4.Pin_0, S4.1, S4.3

custom parts:
  KEYPAD 4x4: Matrix keypad 16 buttons, 4 rows x 4 columns
  H-Bridge with L298N: h-bridge
