# Fritzing sketch correioF (saved by Fritzing 0.9.3b)
breadboards: 1

parts:
  Part3 = RFID-RC522-v2
  U1 = LCD-16X2 [package=lcd-16x2]
  R1 = Resistor [tolerance=±5% resistance=220 package=THT]
  R2 = Resistor [tolerance=±5% resistance=220 package=THT]
  S1 = Pushbutton [package="[THT]"]
  S2 = Pushbutton [package="[THT]"]
  R3 = Resistor [tolerance=±5% resistance=220 package=THT]
  R4 = Resistor [tolerance=±5% resistance=220 package=THT]
  LED1 = LED - 5mm [color="Red (633nm)" package="5 mm [THT]"]
  LED2 = LED - 5mm [color="Green (555nm)" package="5 mm [THT]"]
  Componente1 = Arduino Mega 2560 (Rev3)

nets:
  N1: Part3.SDA, Componente1.D12_PWM
  N2: Part3.SCK, Componente1.D30
  N3: Part3.MOSI, Componente1.D11_PWM
  N4: Part3.MISO, Componente1.D13_PWM
  N5: Part3.IRQ, Part3.GND
  N6: Part3.RST, Componente1.D34
  N7: Part3.3_3V, Componente1.3V3
  VSS: U1.VSS, R1.Pin_0, R2.Pin_0, R3.Pin_1, R4.Pin_0, Componente1.GND
  VDD: U1.VDD, Componente1.5V
  N8: R1.Pin_1, LED1.cathode
  N9: R2.Pin_1, LED2.cathode
  N10: S1.Pin_1, S1.Pin_2, S1.Pin_3, S1.Pin_4, R4.Pin_1, Componente1.D42
  N11: S2.Pin_1, S2.Pin_2, S2.Pin_3, S2.Pin_4, R3.Pin_0, Componente1.D38

custom parts:
  RFID-RC522-v2: A simple China made RFID-RC522 Reader; do check the pin labels, as this is a MFRC522 based clone.
